// Logisim project 26-bit-multicycle-mips.circ as structural Verilog: 21 circuits, main circuit CPU
module _16x26_RegFile (
  input  WEN,
  input  [3:0] ReadReg1,
  input  [3:0] ReadReg2,
  input  [3:0] WriteReg,
  input  [25:0] Write_Data,
  input  Clk,
  output [25:0] ReadData1,
  output [25:0] ReadData2
);

  wire decoder_1_out0, decoder_1_out1, decoder_1_out2, decoder_1_out3, decoder_1_out4, decoder_1_out5,
       decoder_1_out6, decoder_1_out7, decoder_1_out8, decoder_1_out9, decoder_1_out10, decoder_1_out11,
       decoder_1_out12, decoder_1_out13, decoder_1_out14, decoder_1_out15;
  wire [25:0] Reg0_q, Reg1_q, Reg2_q, Reg3_q, Reg4_q, Reg5_q, Reg6_q, Reg7_q, Reg8_q, Reg9_q, Reg10_q,
       Reg11_q, Reg12_q, Reg13_q, Reg14_q, Reg15_q;

  Decoder #(.select(4), .disabled(0)) decoder_1 (
    .out0(decoder_1_out0), .out1(decoder_1_out1), .out2(decoder_1_out2), .out3(decoder_1_out3),
    .out4(decoder_1_out4), .out5(decoder_1_out5), .out6(decoder_1_out6), .out7(decoder_1_out7),
    .out8(decoder_1_out8), .out9(decoder_1_out9), .out10(decoder_1_out10), .out11(decoder_1_out11),
    .out12(decoder_1_out12), .out13(decoder_1_out13), .out14(decoder_1_out14), .out15(decoder_1_out15),
    .sel(WriteReg), .en(WEN));
  Register #(.width(26)) Reg0 (.D(Write_Data), .en(decoder_1_out0), .Q(Reg0_q), .clk(Clk));  // open: clr
  Register #(.width(26)) Reg4 (.D(Write_Data), .en(decoder_1_out4), .Q(Reg4_q), .clk(Clk));  // open: clr
  Register #(.width(26)) Reg8 (.D(Write_Data), .en(decoder_1_out8), .Q(Reg8_q), .clk(Clk));  // open: clr
  Register #(.width(26)) Reg12 (.D(Write_Data), .en(decoder_1_out12), .Q(Reg12_q), .clk(Clk));  // open: clr
  Register #(.width(26)) Reg1 (.D(Write_Data), .en(decoder_1_out1), .Q(Reg1_q), .clk(Clk));  // open: clr
  Register #(.width(26)) Reg5 (.D(Write_Data), .en(decoder_1_out5), .Q(Reg5_q), .clk(Clk));  // open: clr
  Register #(.width(26)) Reg9 (.D(Write_Data), .en(decoder_1_out9), .Q(Reg9_q), .clk(Clk));  // open: clr
  Register #(.width(26)) Reg2 (.D(Write_Data), .en(decoder_1_out2), .Q(Reg2_q), .clk(Clk));  // open: clr
  Register #(.width(26)) Reg6 (.D(Write_Data), .en(decoder_1_out6), .Q(Reg6_q), .clk(Clk));  // open: clr
  Register #(.width(26)) Reg10 (.D(Write_Data), .en(decoder_1_out10), .Q(Reg10_q), .clk(Clk));  // open: clr
  Register #(.width(26)) Reg14 (.D(Write_Data), .en(decoder_1_out14), .Q(Reg14_q), .clk(Clk));  // open: clr
  Register #(.width(26)) Reg13 (.D(Write_Data), .en(decoder_1_out13), .Q(Reg13_q), .clk(Clk));  // open: clr
  Register #(.width(26)) Reg3 (.D(Write_Data), .en(decoder_1_out3), .Q(Reg3_q), .clk(Clk));  // open: clr
  Register #(.width(26)) Reg7 (.D(Write_Data), .en(decoder_1_out7), .Q(Reg7_q), .clk(Clk));  // open: clr
  Register #(.width(26)) Reg11 (.D(Write_Data), .en(decoder_1_out11), .Q(Reg11_q), .clk(Clk));  // open: clr
  Register #(.width(26)) Reg15 (.D(Write_Data), .en(decoder_1_out15), .Q(Reg15_q), .clk(Clk));  // open: clr
  Multiplexer #(.select(4), .width(26), .disabled(0)) multiplexer_1 (
    .in0(Reg0_q), .in1(Reg1_q), .in2(Reg2_q), .in3(Reg3_q), .in4(Reg4_q), .in5(Reg5_q), .in6(Reg6_q),
    .in7(Reg7_q), .in8(Reg8_q), .in9(Reg9_q), .in10(Reg10_q), .in11(Reg11_q), .in12(Reg12_q), .in13(Reg13_q),
    .in14(Reg14_q), .in15(Reg15_q), .out(ReadData2), .sel(ReadReg2));  // open: en
  Multiplexer #(.select(4), .width(26), .disabled(0)) multiplexer_2 (
    .in0(Reg0_q), .in1(Reg1_q), .in2(Reg2_q), .in3(Reg3_q), .in4(Reg4_q), .in5(Reg5_q), .in6(Reg6_q),
    .in7(Reg7_q), .in8(Reg7_q), .in9(Reg8_q), .in10(Reg10_q), .in11(Reg11_q), .in12(Reg12_q), .in13(Reg13_q),
    .in14(Reg14_q), .in15(Reg15_q), .out(ReadData1), .sel(ReadReg1));  // open: en
endmodule

module ALU (
  input  [4:0] ALU_Control,
  input  [25:0] a,
  input  [25:0] b,
  output zero,
  output [25:0] out_5
);

  wire comparator_1_eq, comparator_1_gt, comparator_1_lt;
  wire [25:0] adder_1_out, and_1_out, bit_extender_1_out, bit_extender_2_out, bit_extender_3_out,
       divider_1_out, divider_1_rem, multiplier_1_cout, multiplier_1_out, not_1_out, not_2_out, not_3_out,
       not_4_out, not_5_out, or_1_out, or_2_out, or_3_out, shifter_1_out, shifter_2_out, subtractor_1_out,
       xor_1_out;
  wire [25:1] xnor_1_out;

  assign and_1_out = a & b;  // AND_Gate and_1, 26 bits wide
  assign or_1_out = a | b;  // OR_Gate or_1, 26 bits wide
  Adder #(.width(26)) adder_1 (.a(a), .b(b), .out(adder_1_out));  // open: cin, cout
  Subtractor #(.width(26)) subtractor_1 (.a(a), .b(b), .out(subtractor_1_out));  // open: bin, bout
  Comparator #(.width(26)) comparator_1 (
    .a(a), .b(b), .gt(comparator_1_gt), .eq(comparator_1_eq), .lt(comparator_1_lt));
  assign xor_1_out = a ^ b;  // XOR_Gate xor_1, 26 bits wide
  assign bit_extender_1_out = {{25{1'b0}}, comparator_1_gt};  // Bit_Extender bit_extender_1
  assign bit_extender_2_out = {{25{1'b0}}, comparator_1_lt};  // Bit_Extender bit_extender_2
  assign not_1_out = ~xor_1_out;  // NOT_Gate not_1, 26 bits wide
  assign not_2_out = ~or_1_out;  // NOT_Gate not_2, 26 bits wide
  assign not_3_out = ~and_1_out;  // NOT_Gate not_3, 26 bits wide
  assign not_4_out = ~b;  // NOT_Gate not_4, 26 bits wide
  assign not_5_out = ~b;  // NOT_Gate not_5, 26 bits wide
  assign bit_extender_3_out = {{25{1'b0}}, comparator_1_eq};  // Bit_Extender bit_extender_3
  assign or_2_out = bit_extender_3_out | bit_extender_2_out;  // OR_Gate or_2, 26 bits wide
  Shifter #(.width(26)) shifter_1 (.in(a), .\dist (b[4:0]), .out(shifter_1_out));
  Shifter #(.width(26), .shift("lr")) shifter_2 (.in(a), .\dist (b[4:0]), .out(shifter_2_out));
  Multiplier #(.width(26)) multiplier_1 (.a(a), .b(b), .out(multiplier_1_out), .cout(multiplier_1_cout));  // open: cin
  Divider #(.width(26)) divider_1 (.a(a), .b(b), .out(divider_1_out), .rem(divider_1_rem));  // open: upper
  assign or_3_out = bit_extender_1_out | bit_extender_3_out;  // OR_Gate or_3, 26 bits wide
  Multiplexer #(.select(5), .width(26)) multiplexer_1 (
    .in0(and_1_out), .in1(or_1_out), .in2(adder_1_out), .in3(subtractor_1_out), .in4(bit_extender_2_out),
    .in5(xor_1_out), .in6(not_1_out), .in7(not_2_out), .in8(not_3_out), .in9(a), .in10(b), .in11(not_4_out),
    .in12(not_5_out), .in13(bit_extender_1_out), .in14(or_2_out), .in15(or_3_out), .in16(shifter_1_out),
    .in17(shifter_2_out), .in18(multiplier_1_out), .in19(multiplier_1_cout), .in20(divider_1_out),
    .in21(divider_1_rem), .in22({26{1'b0}}), .in23({26{1'b0}}), .in24({26{1'b0}}), .in25({26{1'b0}}),
    .in26({26{1'b0}}), .in27({26{1'b0}}), .in28({26{1'b0}}), .in29({26{1'b0}}), .in30({26{1'b0}}),
    .in31({26{1'b0}}), .out(out_5), .sel(ALU_Control));  // open: en
  assign {xnor_1_out, zero} = ~(out_5 ^ {26{1'b0}});  // XNOR_Gate xnor_1, 26 bits wide
endmodule

module _26bitROM (
  input  [25:0] Read_address,
  output [25:0] Instruction
);

  wire decoder_1_out0, decoder_1_out1, decoder_1_out2, decoder_1_out3;
  wire [25:0] rom_1_data, rom_2_data, rom_3_data, rom_4_data;

  Decoder #(.select(2)) decoder_1 (
    .out0(decoder_1_out0), .out1(decoder_1_out1), .out2(decoder_1_out2), .out3(decoder_1_out3),
    .sel(Read_address[25:24]));  // open: en
  ROM #(.addrWidth(24), .dataWidth(26)) rom_1 (.addr(Read_address[23:0]), .data(rom_1_data), .sel(decoder_1_out0));
  ROM #(.addrWidth(24), .dataWidth(26)) rom_2 (.addr(Read_address[23:0]), .data(rom_2_data), .sel(decoder_1_out1));
  ROM #(.addrWidth(24), .dataWidth(26)) rom_3 (.addr(Read_address[23:0]), .data(rom_3_data), .sel(decoder_1_out2));
  ROM #(.addrWidth(24), .dataWidth(26)) rom_4 (.addr(Read_address[23:0]), .data(rom_4_data), .sel(decoder_1_out3));
  Multiplexer #(.select(2), .width(26)) multiplexer_1 (
    .in0(rom_1_data), .in1(rom_2_data), .in2(rom_3_data), .in3(rom_4_data), .out(Instruction),
    .sel(Read_address[25:24]));  // open: en

  // Notes on the sheet:
  //   contents of rom_1 (hex, n*v repeats v):
  //   2004005 2008003 48403 2c04000 c04000 5404 1140001 800002
endmodule

module _26bitRAM (
  input  MemWrite,
  input  [25:0] Address,
  input  [25:0] Write_Data,
  input  Clk,
  input  MemRead,
  output [25:0] Read_Data
);

  wire decoder_1_out0, decoder_1_out1, decoder_1_out2, decoder_1_out3;
  wire [25:0] ram_1_data, ram_2_data, ram_3_data, ram_4_data;

  Decoder #(.select(2)) decoder_1 (
    .out0(decoder_1_out0), .out1(decoder_1_out1), .out2(decoder_1_out2), .out3(decoder_1_out3),
    .sel(Address[25:24]));  // open: en
  RAM #(.addrWidth(24), .dataWidth(26), .bus("separate")) ram_1 (
    .addr(Address[23:0]), .din(Write_Data), .data(ram_1_data), .str(MemWrite), .sel(decoder_1_out0),
    .clk(Clk), .ld(MemRead));  // open: clr
  RAM #(.addrWidth(24), .dataWidth(26), .bus("separate")) ram_2 (
    .addr(Address[23:0]), .din(Write_Data), .data(ram_2_data), .str(MemWrite), .sel(decoder_1_out1),
    .clk(Clk), .ld(MemRead));  // open: clr
  RAM #(.addrWidth(24), .dataWidth(26), .bus("separate")) ram_3 (
    .addr(Address[23:0]), .din(Write_Data), .data(ram_3_data), .str(MemWrite), .sel(decoder_1_out2),
    .clk(Clk), .ld(MemRead));  // open: clr
  RAM #(.addrWidth(24), .dataWidth(26), .bus("separate")) ram_4 (
    .addr(Address[23:0]), .din(Write_Data), .data(ram_4_data), .str(MemWrite), .sel(decoder_1_out3),
    .clk(Clk), .ld(MemRead));  // open: clr
  Multiplexer #(.select(2), .width(26)) multiplexer_1 (
    .in0(ram_1_data), .in1(ram_2_data), .in2(ram_3_data), .in3(ram_4_data), .out(Read_Data),
    .sel(Address[25:24]));  // open: en
endmodule

module CPU (
);

  wire alu_1_zero, and_1_out, clock_1_out, control_1_alusrca, control_1_iord, control_1_irwrite,
       control_1_memread, control_1_memtoreg, control_1_memwrite, control_1_pcwrite, control_1_pcwrite_cond,
       control_1_regdst, control_1_regwrite, or_1_out;
  wire [1:0] control_1_aluop, control_1_alusrcb, control_1_pcsource;
  wire [3:0] control_1_stateoutput, multiplexer_2_out, State_Register_q;
  wire [4:0] alucontrol_1_out_3;
  wire [22:0] Instruction_Register_q;
  wire [25:0] A_q, adder_1_out, alu_1_out_5, ALUOut_q, B_q, bit_extender_1_out, Memory_Data_Register_q,
       multiplexer_1_out, multiplexer_3_out, multiplexer_4_out, multiplexer_5_out, multiplexer_6_out,
       n16x26_regfile_1_readdata1, n16x26_regfile_1_readdata2, n26bitram_1_read_data, PC_q;
  wire [25:23] Instruction_Register_q_2;

  Register #(.width(26)) PC (.D(multiplexer_6_out), .en(or_1_out), .Q(PC_q), .clk(clock_1_out));  // open: clr
  Clock clock_1 (.out(clock_1_out));
  or or_1 (or_1_out, and_1_out, control_1_pcwrite);
  Multiplexer #(.width(26)) multiplexer_1 (
    .in0(PC_q), .in1(ALUOut_q), .out(multiplexer_1_out), .sel(control_1_iord));  // open: en
  _26bitRAM u_26bitram_1 (
    .MemWrite(control_1_memwrite), .Address(multiplexer_1_out), .Write_Data(B_q),
    .MemRead(control_1_memread), .Clk(clock_1_out), .Read_Data(n26bitram_1_read_data));
  and and_1 (and_1_out, control_1_pcwrite_cond, alu_1_zero);
  Register #(.width(26)) Instruction_Register (
    .D(n26bitram_1_read_data), .en(control_1_irwrite),
    .Q({Instruction_Register_q_2, Instruction_Register_q}), .clk(clock_1_out));  // open: clr
  Register #(.width(26)) Memory_Data_Register (
    .D(n26bitram_1_read_data), .Q(Memory_Data_Register_q), .clk(clock_1_out));  // open: en, clr
  Control control_1 (
    .OpCode({Instruction_Register_q_2, Instruction_Register_q[22]}), .State(State_Register_q),
    .StateOutput(control_1_stateoutput), .RegDst(control_1_regdst), .RegWrite(control_1_regwrite),
    .ALUSrcA(control_1_alusrca), .MemRead(control_1_memread), .MemWrite(control_1_memwrite),
    .MemToReg(control_1_memtoreg), .IorD(control_1_iord), .IRWrite(control_1_irwrite),
    .PCWrite(control_1_pcwrite), .PCWrite_Cond(control_1_pcwrite_cond), .ALUSrcB(control_1_alusrcb),
    .ALUOp(control_1_aluop), .PCSource(control_1_pcsource));
  Multiplexer #(.width(4)) multiplexer_2 (
    .in0(Instruction_Register_q[17:14]), .in1(Instruction_Register_q[13:10]), .out(multiplexer_2_out),
    .sel(control_1_regdst));  // open: en
  Multiplexer #(.width(26)) multiplexer_3 (
    .in0(ALUOut_q), .in1(Memory_Data_Register_q), .out(multiplexer_3_out), .sel(control_1_memtoreg));  // open: en
  assign bit_extender_1_out = {{12{Instruction_Register_q[13]}}, Instruction_Register_q[13:0]};  // Bit_Extender bit_extender_1
  Register #(.width(4)) State_Register (
    .D(control_1_stateoutput), .Q(State_Register_q), .clk(clock_1_out));  // open: en, clr
  _16x26_RegFile u_16x26_regfile_1 (
    .ReadReg1(Instruction_Register_q[21:18]), .ReadReg2(Instruction_Register_q[17:14]),
    .WriteReg(multiplexer_2_out), .ReadData1(n16x26_regfile_1_readdata1),
    .ReadData2(n16x26_regfile_1_readdata2), .WEN(control_1_regwrite), .Clk(clock_1_out),
    .Write_Data(multiplexer_3_out));
  Multiplexer #(.width(26)) multiplexer_4 (
    .in0(PC_q), .in1(A_q), .out(multiplexer_4_out), .sel(control_1_alusrca));  // open: en
  Register #(.width(26)) A (.D(n16x26_regfile_1_readdata1), .Q(A_q), .clk(clock_1_out));  // open: en, clr
  Register #(.width(26)) B (.D(n16x26_regfile_1_readdata2), .Q(B_q), .clk(clock_1_out));  // open: en, clr
  Adder #(.width(26)) adder_1 (.a(PC_q), .b(bit_extender_1_out), .out(adder_1_out));  // open: cin, cout
  Multiplexer #(.select(2), .width(26)) multiplexer_5 (
    .in0(B_q), .in1(26'h1), .in2(bit_extender_1_out), .in3(adder_1_out), .out(multiplexer_5_out),
    .sel(control_1_alusrcb));  // open: en
  ALUControl alucontrol_1 (.in_1(control_1_aluop), .in_2(Instruction_Register_q[4:0]), .out_3(alucontrol_1_out_3));
  Register #(.width(26)) ALUOut (.D(alu_1_out_5), .Q(ALUOut_q), .clk(clock_1_out));  // open: en, clr
  ALU alu_1 (
    .a(multiplexer_4_out), .b(multiplexer_5_out), .out_5(alu_1_out_5), .ALU_Control(alucontrol_1_out_3),
    .zero(alu_1_zero));
  Multiplexer #(.select(2), .width(26)) multiplexer_6 (
    .in0(alu_1_out_5), .in1(ALUOut_q), .in2({PC_q[25:23], Instruction_Register_q}), .out(multiplexer_6_out),
    .sel(control_1_pcsource));  // open: in3, en
endmodule

module Control (
  input  [3:0] OpCode,
  input  [3:0] State,
  output [1:0] PCSource,
  output RegDst,
  output RegWrite,
  output ALUSrcA,
  output [1:0] ALUSrcB,
  output MemRead,
  output MemWrite,
  output MemToReg,
  output IorD,
  output IRWrite,
  output PCWrite,
  output PCWrite_Cond,
  output [3:0] StateOutput,
  output [1:0] ALUOp
);

  wire alusrcasub_1_alusrca, and_1_out, comparator_1_eq, comparator_2_eq;

  Comparator #(.width(4)) comparator_1 (.a(OpCode), .b(4'b0100), .eq(comparator_1_eq));  // open: gt, lt
  Comparator #(.width(4)) comparator_2 (.a(4'b0001), .b(State), .eq(comparator_2_eq));  // open: gt, lt
  and and_1 (and_1_out, comparator_1_eq, comparator_2_eq);
  PCSourceSub pcsourcesub_1 (
    .PCSource1(PCSource[1]), .PCSource0(PCSource[0]), .State3(State[3]), .State2(State[2]),
    .State1(State[1]), .State0(State[0]));
  RegDstSub regdstsub_1 (.State3(State[3]), .RegDst(RegDst), .State2(State[2]), .State1(State[1]), .State0(State[0]));
  ALUSrcASub alusrcasub_1 (
    .State3(State[3]), .State2(State[2]), .State1(State[1]), .State0(State[0]), .ALUSrcA(alusrcasub_1_alusrca));
  ALUSrcBSub alusrcbsub_1 (
    .State3(State[3]), .State2(State[2]), .ALUSrcB1(ALUSrcB[1]), .State1(State[1]), .State0(State[0]),
    .ALUSrcB0(ALUSrcB[0]));
  MemReadSub memreadsub_1 (
    .State3(State[3]), .State2(State[2]), .State1(State[1]), .State0(State[0]), .MemRead(MemRead));
  MemWriteSub memwritesub_1 (
    .State3(State[3]), .State2(State[2]), .State1(State[1]), .State0(State[0]), .MemWrite(MemWrite));
  MemToRegSub memtoregsub_1 (
    .Stat3(State[3]), .State2(State[2]), .State1(State[1]), .State0(State[0]), .MemToReg(MemToReg));
  IorDSub iordsub_1 (.State3(State[3]), .State2(State[2]), .State1(State[1]), .State0(State[0]), .IorD(IorD));
  IRWriteSub irwritesub_1 (
    .State3(State[3]), .State2(State[2]), .State1(State[1]), .State0(State[0]), .IRWrite(IRWrite));
  PCWriteSub pcwritesub_1 (
    .State3(State[3]), .State2(State[2]), .State1(State[1]), .State0(State[0]), .PCWrite(PCWrite));
  PCWriteCondSub pcwritecondsub_1 (
    .State3(State[3]), .State2(State[2]), .State1(State[1]), .State0(State[0]), .PCWriteCond(PCWrite_Cond));
  ALUOpSub aluopsub_1 (
    .State3(State[3]), .ALUOp1(ALUOp[1]), .State2(State[2]), .State1(State[1]), .ALUOp0(ALUOp[0]),
    .State0(State[0]));
  RegWriteSub regwritesub_1 (
    .State3(State[3]), .State2(State[2]), .State1(State[1]), .State0(State[0]), .RegWrite(RegWrite));
  or or_1 (ALUSrcA, alusrcasub_1_alusrca, and_1_out);
  StateOutputSub stateoutputsub_1 (
    .State3(State[3]), .State2(State[2]), .State1(State[1]), .State0(State[0]),
    .StateOutput3(StateOutput[3]), .OpCode3(OpCode[3]), .OpCode2(OpCode[2]), .Opcode1(OpCode[1]),
    .OpCode0(OpCode[0]), .StateOutput2(StateOutput[2]), .StateOutput1(StateOutput[1]),
    .StateOutput0(StateOutput[0]));

  // Notes on the sheet:
  //   A bandaid solution to branch problem
endmodule

module ALUControl (
  input  [1:0] in_1,
  input  [4:0] in_2,
  output [4:0] out_3
);

  wire and_4_out, not_1_out;

  and and_1 (out_3[4], in_1[1], in_2[4]);
  and and_2 (out_3[3], in_1[1], in_2[3]);
  and and_3 (out_3[2], in_1[1], in_2[2]);
  not not_1 (not_1_out, in_1[1]);
  or or_1 (out_3[1], not_1_out, in_2[1]);
  and and_4 (and_4_out, in_1[1], in_2[0]);
  or or_2 (out_3[0], in_1[0], and_4_out);
endmodule

module PCSourceSub (
  input  State3,
  input  State2,
  input  State1,
  input  State0,
  output PCSource1,
  output PCSource0
);

  wire not_1_out;

  and and_1 (PCSource1, State3, State0);
  and and_2 (PCSource0, State3, not_1_out);
  not not_1 (not_1_out, State0);
endmodule

module RegDstSub (
  input  State3,
  input  State2,
  input  State1,
  input  State0,
  output RegDst
);

  wire and_1_out, and_2_out, not_1_out, not_2_out;

  not not_1 (not_1_out, State1);
  not not_2 (not_2_out, State0);
  and and_1 (and_1_out, State2, State1, State0);
  or or_1 (RegDst, and_1_out, and_2_out);
  and and_2 (and_2_out, State3, State2, not_1_out, not_2_out);
endmodule

module ALUSrcASub (
  input  State3,
  input  State2,
  input  State1,
  input  State0,
  output ALUSrcA
);

  wire and_1_out, and_2_out, and_3_out, and_4_out, not_1_out, not_2_out, not_3_out, not_4_out, not_5_out,
       not_6_out;

  not not_1 (not_1_out, State3);
  and and_1 (and_1_out, not_1_out, State1);
  not not_2 (not_2_out, State3);
  and and_2 (and_2_out, not_2_out, State2);
  not not_3 (not_3_out, State2);
  and and_3 (and_3_out, State3, not_3_out, not_4_out);
  not not_4 (not_4_out, State1);
  and and_4 (and_4_out, State3, not_5_out, not_6_out);
  not not_5 (not_5_out, State2);
  not not_6 (not_6_out, State0);
  or or_1 (ALUSrcA, and_1_out, and_2_out, and_3_out, and_4_out);
endmodule

module ALUSrcBSub (
  input  State3,
  input  State2,
  input  State1,
  input  State0,
  output ALUSrcB1,
  output ALUSrcB0
);

  wire and_1_out, and_2_out, and_3_out, and_4_out, and_5_out, not_1_out, not_2_out, not_3_out, not_4_out,
       not_5_out, not_6_out;

  not not_1 (not_1_out, State2);
  and and_1 (and_1_out, not_1_out, State0);
  not not_2 (not_2_out, State2);
  and and_2 (and_2_out, not_2_out, State1);
  and and_3 (and_3_out, State2, not_3_out);
  not not_3 (not_3_out, State1);
  not not_4 (not_4_out, State3);
  not not_5 (not_5_out, State2);
  and and_4 (and_4_out, not_4_out, not_5_out, not_6_out);
  not not_6 (not_6_out, State1);
  and and_5 (and_5_out, State3, State0);
  or or_1 (ALUSrcB1, and_1_out, and_2_out, and_3_out);
  or or_2 (ALUSrcB0, and_4_out, and_5_out);
endmodule

module MemReadSub (
  input  State3,
  input  State2,
  input  State1,
  input  State0,
  output MemRead
);

  wire and_1_out, and_2_out, not_1_out, not_2_out, not_3_out, not_4_out, not_5_out;

  not not_1 (not_1_out, State3);
  not not_2 (not_2_out, State2);
  not not_3 (not_3_out, State1);
  not not_4 (not_4_out, State0);
  not not_5 (not_5_out, State2);
  and and_1 (and_1_out, not_1_out, not_2_out, not_3_out, not_4_out);
  or or_1 (MemRead, and_1_out, and_2_out);
  and and_2 (and_2_out, not_5_out, State1, State0);
endmodule

module MemWriteSub (
  input  State3,
  input  State2,
  input  State1,
  input  State0,
  output MemWrite
);

  wire not_1_out;

  not not_1 (not_1_out, State1);
  and and_1 (MemWrite, State2, not_1_out, State0);
endmodule

module MemToRegSub (
  input  Stat3,
  input  State2,
  input  State1,
  input  State0,
  output MemToReg
);

  wire not_1_out, not_2_out;

  not not_1 (not_1_out, State1);
  and and_1 (MemToReg, State2, not_1_out, not_2_out);
  not not_2 (not_2_out, State0);
endmodule

module IorDSub (
  input  State3,
  input  State2,
  input  State1,
  input  State0,
  output IorD
);

  wire and_1_out, and_2_out, not_1_out, not_2_out, not_3_out, not_4_out;

  not not_1 (not_1_out, State3);
  not not_2 (not_2_out, State2);
  not not_3 (not_3_out, State3);
  not not_4 (not_4_out, State1);
  and and_1 (and_1_out, not_1_out, not_2_out, State1, State0);
  or or_1 (IorD, and_1_out, and_2_out);
  and and_2 (and_2_out, not_3_out, State2, not_4_out, State0);
endmodule

module IRWriteSub (
  input  State3,
  input  State2,
  input  State1,
  input  State0,
  output IRWrite
);

  wire not_1_out, not_2_out, not_3_out, not_4_out;

  not not_1 (not_1_out, State3);
  not not_2 (not_2_out, State2);
  not not_3 (not_3_out, State1);
  not not_4 (not_4_out, State0);
  and and_1 (IRWrite, not_1_out, not_2_out, not_3_out, not_4_out);
endmodule

module PCWriteSub (
  input  State3,
  input  State2,
  input  State1,
  input  State0,
  output PCWrite
);

  wire and_1_out, and_2_out, and_3_out, not_1_out, not_2_out, not_3_out, not_4_out, not_5_out, not_6_out,
       not_7_out, not_8_out;

  not not_1 (not_1_out, State3);
  not not_2 (not_2_out, State2);
  not not_3 (not_3_out, State1);
  not not_4 (not_4_out, State0);
  not not_5 (not_5_out, State2);
  not not_6 (not_6_out, State1);
  not not_7 (not_7_out, State1);
  not not_8 (not_8_out, State0);
  and and_1 (and_1_out, not_1_out, not_2_out, not_3_out, not_4_out);
  and and_2 (and_2_out, State3, not_5_out, not_6_out, State0);
  or or_1 (PCWrite, and_1_out, and_2_out, and_3_out);
  and and_3 (and_3_out, State3, State2, not_7_out, not_8_out);
endmodule

module PCWriteCondSub (
  input  State3,
  input  State2,
  input  State1,
  input  State0,
  output PCWriteCond
);

  wire not_1_out;

  and and_1 (PCWriteCond, State3, not_1_out);
  not not_1 (not_1_out, State0);
endmodule

module StateOutputSub (
  input  State3,
  input  State2,
  input  State1,
  input  State0,
  input  OpCode3,
  input  OpCode2,
  input  Opcode1,
  input  OpCode0,
  output StateOutput3,
  output StateOutput2,
  output StateOutput1,
  output StateOutput0
);

  wire and_1_out, and_2_out, and_3_out, and_4_out, and_5_out, and_6_out, and_7_out, and_8_out, and_9_out,
       and_10_out, and_11_out, and_12_out, and_13_out, and_14_out, and_15_out, and_16_out, and_17_out,
       and_18_out, not_1_out, not_2_out, not_3_out, not_4_out, not_5_out, not_6_out, not_7_out, not_8_out,
       not_9_out, not_10_out, not_11_out, not_12_out, not_13_out, not_14_out, not_15_out, not_16_out,
       not_17_out, not_18_out, not_19_out, not_20_out, not_21_out, not_22_out, not_23_out, not_24_out,
       not_25_out, not_26_out, not_27_out, not_28_out, not_29_out, not_30_out, not_31_out, not_32_out,
       not_33_out, not_34_out, not_35_out, not_36_out, not_37_out, not_38_out, not_39_out, not_40_out,
       not_41_out, not_42_out, not_43_out, not_44_out, not_45_out, not_46_out;

  not not_1 (not_1_out, State3);
  not not_2 (not_2_out, State2);
  not not_3 (not_3_out, OpCode0);
  not not_4 (not_4_out, State3);
  not not_5 (not_5_out, State2);
  not not_6 (not_6_out, State3);
  not not_7 (not_7_out, State2);
  not not_8 (not_8_out, State1);
  not not_9 (not_9_out, OpCode0);
  not not_10 (not_10_out, State2);
  not not_11 (not_11_out, State0);
  not not_12 (not_12_out, State3);
  not not_13 (not_13_out, State2);
  not not_14 (not_14_out, OpCode3);
  not not_15 (not_15_out, OpCode2);
  not not_16 (not_16_out, Opcode1);
  not not_17 (not_17_out, State3);
  not not_18 (not_18_out, State2);
  not not_19 (not_19_out, OpCode2);
  not not_20 (not_20_out, Opcode1);
  not not_21 (not_21_out, State3);
  not not_22 (not_22_out, State0);
  not not_23 (not_23_out, State3);
  not not_24 (not_24_out, State2);
  not not_25 (not_25_out, State0);
  not not_26 (not_26_out, State3);
  not not_27 (not_27_out, State2);
  not not_28 (not_28_out, OpCode2);
  not not_29 (not_29_out, Opcode1);
  not not_30 (not_30_out, State3);
  not not_31 (not_31_out, State2);
  not not_32 (not_32_out, State1);
  not not_33 (not_33_out, OpCode2);
  not not_34 (not_34_out, State0);
  not not_35 (not_35_out, OpCode3);
  not not_36 (not_36_out, State0);
  not not_37 (not_37_out, State0);
  not not_38 (not_38_out, State3);
  not not_39 (not_39_out, State2);
  not not_40 (not_40_out, State0);
  not not_41 (not_41_out, State3);
  not not_42 (not_42_out, State2);
  not not_43 (not_43_out, OpCode0);
  not not_44 (not_44_out, State3);
  not not_45 (not_45_out, State2);
  not not_46 (not_46_out, State0);
  and and_1 (and_1_out, not_1_out, not_2_out, State0, Opcode1, not_3_out);
  and and_2 (and_2_out, not_4_out, not_5_out, State0, OpCode2);
  and and_3 (and_3_out, not_6_out, not_7_out, not_8_out, State0, OpCode3, not_9_out);
  and and_4 (and_4_out, State3, not_10_out, State1, not_11_out);
  and and_5 (and_5_out, not_12_out, not_13_out, State0, not_14_out, not_15_out, not_16_out);
  and and_6 (and_6_out, not_17_out, not_18_out, State0, not_19_out, not_20_out, OpCode0);
  and and_7 (and_7_out, not_21_out, State1, not_22_out, OpCode3);
  and and_8 (and_8_out, not_23_out, not_24_out, State1, State0);
  and and_9 (and_9_out, State2, State1, not_25_out);
  and and_10 (and_10_out, not_26_out, not_27_out, State0, not_28_out, not_29_out);
  and and_11 (and_11_out, not_30_out, not_31_out, not_32_out, State0, not_33_out, OpCode0);
  and and_12 (and_12_out, State1, not_34_out, not_35_out);
  and and_13 (and_13_out, State2, State1, not_36_out);
  and and_14 (and_14_out, State3, State1, not_37_out);
  and and_15 (and_15_out, not_38_out, not_39_out, not_40_out);
  and and_16 (and_16_out, not_41_out, not_42_out, Opcode1, not_43_out);
  and and_17 (and_17_out, not_44_out, not_45_out, OpCode2, Opcode1);
  and and_18 (and_18_out, State1, not_46_out);
  or or_1 (StateOutput3, and_1_out, and_2_out, and_3_out, and_4_out);
  or or_2 (StateOutput2, and_5_out, and_6_out, and_7_out, and_8_out, and_9_out);
  or or_3 (StateOutput1, and_10_out, and_11_out, and_12_out, and_13_out, and_14_out);
  or or_4 (StateOutput0, and_15_out, and_16_out, and_17_out, and_18_out);
endmodule

module ALUOpSub (
  input  State3,
  input  State2,
  input  State1,
  input  State0,
  output ALUOp1,
  output ALUOp0
);

  wire and_2_out, and_3_out, not_1_out, not_2_out, not_3_out, not_4_out;

  not not_1 (not_1_out, State3);
  and and_1 (ALUOp1, not_1_out, State2, State1);
  not not_2 (not_2_out, State2);
  not not_3 (not_3_out, State1);
  not not_4 (not_4_out, State0);
  and and_2 (and_2_out, State3, not_2_out, not_3_out, not_4_out);
  or or_1 (ALUOp0, and_2_out, and_3_out);
  and and_3 (and_3_out, State3, State2, State1, State0);
endmodule

module RegWriteSub (
  input  State3,
  input  State2,
  input  State1,
  input  State0,
  output RegWrite
);

  wire and_1_out, and_2_out, and_3_out, not_1_out, not_2_out, not_3_out, not_4_out, not_5_out;

  not not_1 (not_1_out, State3);
  not not_2 (not_2_out, State1);
  not not_3 (not_3_out, State0);
  not not_4 (not_4_out, State3);
  not not_5 (not_5_out, State2);
  and and_1 (and_1_out, not_1_out, State2, not_2_out, not_3_out);
  or or_1 (RegWrite, and_1_out, and_2_out, and_3_out);
  and and_2 (and_2_out, not_4_out, State2, State1, State0);
  and and_3 (and_3_out, State3, not_5_out, State1, State0);
endmodule
