// Logisim project 26-bit-singlecycle-mips.circ as structural Verilog: 7 circuits, main circuit CPU
module _16x26_RegFile (
  input  WEN,
  input  [3:0] ReadReg1,
  input  [3:0] ReadReg2,
  input  [3:0] WriteReg,
  input  [25:0] Write_Data,
  input  Clk,
  output [25:0] ReadData1,
  output [25:0] ReadData2
);

  wire decoder_1_out0, decoder_1_out1, decoder_1_out2, decoder_1_out3, decoder_1_out4, decoder_1_out5,
       decoder_1_out6, decoder_1_out7, decoder_1_out8, decoder_1_out9, decoder_1_out10, decoder_1_out11,
       decoder_1_out12, decoder_1_out13, decoder_1_out14, decoder_1_out15;
  wire [25:0] Reg0_q, Reg1_q, Reg2_q, Reg3_q, Reg4_q, Reg5_q, Reg6_q, Reg7_q, Reg8_q, Reg9_q, Reg10_q,
       Reg11_q, Reg12_q, Reg13_q, Reg14_q, Reg15_q;

  Decoder #(.select(4), .disabled(0)) decoder_1 (
    .out0(decoder_1_out0), .out1(decoder_1_out1), .out2(decoder_1_out2), .out3(decoder_1_out3),
    .out4(decoder_1_out4), .out5(decoder_1_out5), .out6(decoder_1_out6), .out7(decoder_1_out7),
    .out8(decoder_1_out8), .out9(decoder_1_out9), .out10(decoder_1_out10), .out11(decoder_1_out11),
    .out12(decoder_1_out12), .out13(decoder_1_out13), .out14(decoder_1_out14), .out15(decoder_1_out15),
    .sel(WriteReg), .en(WEN));
  Register #(.width(26)) Reg0 (.D(Write_Data), .en(decoder_1_out0), .Q(Reg0_q), .clk(Clk));  // open: clr
  Register #(.width(26)) Reg4 (.D(Write_Data), .en(decoder_1_out4), .Q(Reg4_q), .clk(Clk));  // open: clr
  Register #(.width(26)) Reg8 (.D(Write_Data), .en(decoder_1_out8), .Q(Reg8_q), .clk(Clk));  // open: clr
  Register #(.width(26)) Reg12 (.D(Write_Data), .en(decoder_1_out12), .Q(Reg12_q), .clk(Clk));  // open: clr
  Register #(.width(26)) Reg1 (.D(Write_Data), .en(decoder_1_out1), .Q(Reg1_q), .clk(Clk));  // open: clr
  Register #(.width(26)) Reg5 (.D(Write_Data), .en(decoder_1_out5), .Q(Reg5_q), .clk(Clk));  // open: clr
  Register #(.width(26)) Reg9 (.D(Write_Data), .en(decoder_1_out9), .Q(Reg9_q), .clk(Clk));  // open: clr
  Register #(.width(26)) Reg2 (.D(Write_Data), .en(decoder_1_out2), .Q(Reg2_q), .clk(Clk));  // open: clr
  Register #(.width(26)) Reg6 (.D(Write_Data), .en(decoder_1_out6), .Q(Reg6_q), .clk(Clk));  // open: clr
  Register #(.width(26)) Reg10 (.D(Write_Data), .en(decoder_1_out10), .Q(Reg10_q), .clk(Clk));  // open: clr
  Register #(.width(26)) Reg14 (.D(Write_Data), .en(decoder_1_out14), .Q(Reg14_q), .clk(Clk));  // open: clr
  Register #(.width(26)) Reg13 (.D(Write_Data), .en(decoder_1_out13), .Q(Reg13_q), .clk(Clk));  // open: clr
  Register #(.width(26)) Reg3 (.D(Write_Data), .en(decoder_1_out3), .Q(Reg3_q), .clk(Clk));  // open: clr
  Register #(.width(26)) Reg7 (.D(Write_Data), .en(decoder_1_out7), .Q(Reg7_q), .clk(Clk));  // open: clr
  Register #(.width(26)) Reg11 (.D(Write_Data), .en(decoder_1_out11), .Q(Reg11_q), .clk(Clk));  // open: clr
  Register #(.width(26)) Reg15 (.D(Write_Data), .en(decoder_1_out15), .Q(Reg15_q), .clk(Clk));  // open: clr
  Multiplexer #(.select(4), .width(26), .disabled(0)) multiplexer_1 (
    .in0(Reg0_q), .in1(Reg1_q), .in2(Reg2_q), .in3(Reg3_q), .in4(Reg4_q), .in5(Reg5_q), .in6(Reg6_q),
    .in7(Reg7_q), .in8(Reg8_q), .in9(Reg9_q), .in10(Reg10_q), .in11(Reg11_q), .in12(Reg12_q), .in13(Reg13_q),
    .in14(Reg14_q), .in15(Reg15_q), .out(ReadData2), .sel(ReadReg2));  // open: en
  Multiplexer #(.select(4), .width(26), .disabled(0)) multiplexer_2 (
    .in0(Reg0_q), .in1(Reg1_q), .in2(Reg2_q), .in3(Reg3_q), .in4(Reg4_q), .in5(Reg5_q), .in6(Reg6_q),
    .in7(Reg7_q), .in8(Reg8_q), .in9(Reg9_q), .in10(Reg10_q), .in11(Reg11_q), .in12(Reg12_q), .in13(Reg13_q),
    .in14(Reg14_q), .in15(Reg15_q), .out(ReadData1), .sel(ReadReg1));  // open: en
endmodule

module ALU (
  input  [4:0] ALU_Control,
  input  [25:0] a,
  input  [25:0] b,
  output zero,
  output [25:0] out_5
);

  wire comparator_1_eq, comparator_1_gt, comparator_1_lt;
  wire [25:0] adder_1_out, and_1_out, bit_extender_1_out, bit_extender_2_out, bit_extender_3_out,
       divider_1_out, divider_1_rem, multiplier_1_cout, multiplier_1_out, not_1_out, not_2_out, not_3_out,
       not_4_out, not_5_out, or_1_out, or_2_out, or_3_out, shifter_1_out, shifter_2_out, subtractor_1_out,
       xor_1_out;
  wire [25:1] xnor_1_out;

  assign and_1_out = a & b;  // AND_Gate and_1, 26 bits wide
  assign or_1_out = a | b;  // OR_Gate or_1, 26 bits wide
  Adder #(.width(26)) adder_1 (.a(a), .b(b), .out(adder_1_out));  // open: cin, cout
  Subtractor #(.width(26)) subtractor_1 (.a(a), .b(b), .out(subtractor_1_out));  // open: bin, bout
  Comparator #(.width(26)) comparator_1 (
    .a(a), .b(b), .gt(comparator_1_gt), .eq(comparator_1_eq), .lt(comparator_1_lt));
  assign xor_1_out = a ^ b;  // XOR_Gate xor_1, 26 bits wide
  assign bit_extender_1_out = {{25{1'b0}}, comparator_1_gt};  // Bit_Extender bit_extender_1
  assign bit_extender_2_out = {{25{1'b0}}, comparator_1_lt};  // Bit_Extender bit_extender_2
  assign not_1_out = ~xor_1_out;  // NOT_Gate not_1, 26 bits wide
  assign not_2_out = ~or_1_out;  // NOT_Gate not_2, 26 bits wide
  assign not_3_out = ~and_1_out;  // NOT_Gate not_3, 26 bits wide
  assign not_4_out = ~b;  // NOT_Gate not_4, 26 bits wide
  assign not_5_out = ~b;  // NOT_Gate not_5, 26 bits wide
  assign bit_extender_3_out = {{25{1'b0}}, comparator_1_eq};  // Bit_Extender bit_extender_3
  assign or_2_out = bit_extender_3_out | bit_extender_2_out;  // OR_Gate or_2, 26 bits wide
  Shifter #(.width(26)) shifter_1 (.in(a), .\dist (b[4:0]), .out(shifter_1_out));
  Shifter #(.width(26), .shift("lr")) shifter_2 (.in(a), .\dist (b[4:0]), .out(shifter_2_out));
  Multiplier #(.width(26)) multiplier_1 (.a(a), .b(b), .out(multiplier_1_out), .cout(multiplier_1_cout));  // open: cin
  Divider #(.width(26)) divider_1 (.a(a), .b(b), .out(divider_1_out), .rem(divider_1_rem));  // open: upper
  assign or_3_out = bit_extender_1_out | bit_extender_3_out;  // OR_Gate or_3, 26 bits wide
  Multiplexer #(.select(5), .width(26)) multiplexer_1 (
    .in0(and_1_out), .in1(or_1_out), .in2(adder_1_out), .in3(subtractor_1_out), .in4(bit_extender_2_out),
    .in5(xor_1_out), .in6(not_1_out), .in7(not_2_out), .in8(not_3_out), .in9(a), .in10(b), .in11(not_4_out),
    .in12(not_5_out), .in13(bit_extender_1_out), .in14(or_2_out), .in15(or_3_out), .in16(shifter_1_out),
    .in17(shifter_2_out), .in18(multiplier_1_out), .in19(multiplier_1_cout), .in20(divider_1_out),
    .in21(divider_1_rem), .in22({26{1'b0}}), .in23({26{1'b0}}), .in24({26{1'b0}}), .in25({26{1'b0}}),
    .in26({26{1'b0}}), .in27({26{1'b0}}), .in28({26{1'b0}}), .in29({26{1'b0}}), .in30({26{1'b0}}),
    .in31({26{1'b0}}), .out(out_5), .sel(ALU_Control));  // open: en
  assign {xnor_1_out, zero} = ~(out_5 ^ {26{1'b0}});  // XNOR_Gate xnor_1, 26 bits wide
endmodule

module _26bitROM (
  input  [25:0] Read_address,
  output [25:0] Instruction
);

  wire decoder_1_out0, decoder_1_out1, decoder_1_out2, decoder_1_out3;
  wire [25:0] rom_1_data, rom_2_data, rom_3_data, rom_4_data;

  Decoder #(.select(2)) decoder_1 (
    .out0(decoder_1_out0), .out1(decoder_1_out1), .out2(decoder_1_out2), .out3(decoder_1_out3),
    .sel(Read_address[25:24]));  // open: en
  ROM #(.addrWidth(24), .dataWidth(26)) rom_1 (.addr(Read_address[23:0]), .data(rom_1_data), .sel(decoder_1_out0));
  ROM #(.addrWidth(24), .dataWidth(26)) rom_2 (.addr(Read_address[23:0]), .data(rom_2_data), .sel(decoder_1_out1));
  ROM #(.addrWidth(24), .dataWidth(26)) rom_3 (.addr(Read_address[23:0]), .data(rom_3_data), .sel(decoder_1_out2));
  ROM #(.addrWidth(24), .dataWidth(26)) rom_4 (.addr(Read_address[23:0]), .data(rom_4_data), .sel(decoder_1_out3));
  Multiplexer #(.select(2), .width(26)) multiplexer_1 (
    .in0(rom_1_data), .in1(rom_2_data), .in2(rom_3_data), .in3(rom_4_data), .out(Instruction),
    .sel(Read_address[25:24]));  // open: en

  // Notes on the sheet:
  //   contents of rom_1 (hex, n*v repeats v):
  //   203c0ff 200402b 200801a 48c02 49001 49405 49800 41c02 1838067 2e40000 2e44001 2e48002 2e4c003
  //   2e50004 2e54005 2e58006 2e5c007 80006f 86*0 2fdc000 23fffff 1c9c03 1c2004 1023ffb 1f80000
endmodule

module _26bitRAM (
  input  MemWrite,
  input  [25:0] Address,
  input  [25:0] Write_Data,
  input  Clk,
  input  MemRead,
  output [25:0] Read_Data
);

  wire decoder_1_out0, decoder_1_out1, decoder_1_out2, decoder_1_out3, not_1_out;
  wire [25:0] ram_1_data, ram_2_data, ram_3_data, ram_4_data;

  Decoder #(.select(2)) decoder_1 (
    .out0(decoder_1_out0), .out1(decoder_1_out1), .out2(decoder_1_out2), .out3(decoder_1_out3),
    .sel(Address[25:24]));  // open: en
  not not_1 (not_1_out, Clk);
  RAM #(.addrWidth(24), .dataWidth(26), .bus("separate")) ram_1 (
    .addr(Address[23:0]), .din(Write_Data), .data(ram_1_data), .str(MemWrite), .sel(decoder_1_out0),
    .clk(not_1_out), .ld(MemRead));  // open: clr
  RAM #(.addrWidth(24), .dataWidth(26), .bus("separate")) ram_2 (
    .addr(Address[23:0]), .din(Write_Data), .data(ram_2_data), .str(MemWrite), .sel(decoder_1_out1),
    .clk(not_1_out), .ld(MemRead));  // open: clr
  RAM #(.addrWidth(24), .dataWidth(26), .bus("separate")) ram_3 (
    .addr(Address[23:0]), .din(Write_Data), .data(ram_3_data), .str(MemWrite), .sel(decoder_1_out2),
    .clk(not_1_out), .ld(MemRead));  // open: clr
  RAM #(.addrWidth(24), .dataWidth(26), .bus("separate")) ram_4 (
    .addr(Address[23:0]), .din(Write_Data), .data(ram_4_data), .str(MemWrite), .sel(decoder_1_out3),
    .clk(not_1_out), .ld(MemRead));  // open: clr
  Multiplexer #(.select(2), .width(26)) multiplexer_1 (
    .in0(ram_1_data), .in1(ram_2_data), .in2(ram_3_data), .in3(ram_4_data), .out(Read_Data),
    .sel(Address[25:24]));  // open: en
endmodule

module CPU (
);

  wire alu_1_zero, and_1_out, clock_1_out, control_1_alusrc, control_1_branch, control_1_jal, control_1_jr,
       control_1_jump, control_1_memread, control_1_memtoreg, control_1_memwrite, control_1_regdst,
       control_1_regwrite;
  wire [1:0] control_1_aluop2;
  wire [2:0] adder_1_out_2;
  wire [3:0] multiplexer_2_out;
  wire [4:0] alucontrol_1_out_3;
  wire [8:0] adder_1_out;
  wire [13:0] adder_1_out_3;
  wire [25:0] adder_2_out, alu_1_out_5, bit_extender_1_out, multiplexer_1_out, multiplexer_3_out,
       multiplexer_4_out, multiplexer_5_out, multiplexer_6_out, multiplexer_7_out, multiplexer_8_out,
       n16x26_regfile_1_readdata1, n16x26_regfile_1_readdata2, n26bitram_1_read_data,
       n26bitrom_1_instruction, PC_q;

  Clock clock_1 (.out(clock_1_out));
  Register #(.width(26)) PC (.D(multiplexer_7_out), .Q(PC_q), .clk(clock_1_out));  // open: en, clr
  Adder #(.width(26)) adder_1 (
    .a(26'h1), .b(PC_q), .out({adder_1_out_2, adder_1_out, adder_1_out_3}));  // open: cin, cout
  _26bitROM u_26bitrom_1 (.Read_address(PC_q), .Instruction(n26bitrom_1_instruction));
  Multiplexer #(.width(26)) multiplexer_1 (
    .in0({adder_1_out_2, n26bitrom_1_instruction[22:0]}),
    .in1({adder_1_out_2, adder_1_out, n26bitrom_1_instruction[13:0]}), .out(multiplexer_1_out),
    .sel(control_1_jal));  // open: en
  Control control_1 (
    .RegDst(control_1_regdst), .Jump(control_1_jump), .Branch(control_1_branch), .MemRead(control_1_memread),
    .MemToReg(control_1_memtoreg), .MemWrite(control_1_memwrite), .ALUSrc(control_1_alusrc),
    .RegWrite(control_1_regwrite), .jr(control_1_jr), .jal(control_1_jal), .ALUOp1(control_1_aluop2[1]),
    .ALUOP2(control_1_aluop2[0]), .OpCode(n26bitrom_1_instruction[25:22]));
  Multiplexer #(.width(4)) multiplexer_2 (
    .in0(n26bitrom_1_instruction[17:14]), .in1(n26bitrom_1_instruction[13:10]), .out(multiplexer_2_out),
    .sel(control_1_regdst));  // open: en
  Multiplexer #(.width(26)) multiplexer_3 (
    .in0(multiplexer_8_out), .in1({adder_1_out_2, adder_1_out, adder_1_out_3}), .out(multiplexer_3_out),
    .sel(control_1_jal));  // open: en
  Adder #(.width(26)) adder_2 (
    .a({adder_1_out_2, adder_1_out, adder_1_out_3}), .b(bit_extender_1_out), .out(adder_2_out));  // open: cin, cout
  _16x26_RegFile u_16x26_regfile_1 (
    .ReadReg1(n26bitrom_1_instruction[21:18]), .ReadReg2(n26bitrom_1_instruction[17:14]),
    .WriteReg(multiplexer_2_out), .ReadData1(n16x26_regfile_1_readdata1),
    .ReadData2(n16x26_regfile_1_readdata2), .WEN(control_1_regwrite), .Clk(clock_1_out),
    .Write_Data(multiplexer_3_out));
  assign bit_extender_1_out = {{12{n26bitrom_1_instruction[13]}}, n26bitrom_1_instruction[13:0]};  // Bit_Extender bit_extender_1
  Multiplexer #(.width(26)) multiplexer_4 (
    .in0({adder_1_out_2, adder_1_out, adder_1_out_3}), .in1(adder_2_out), .out(multiplexer_4_out),
    .sel(and_1_out));  // open: en
  and and_1 (and_1_out, control_1_branch, alu_1_zero);
  Multiplexer #(.width(26)) multiplexer_5 (
    .in0(n16x26_regfile_1_readdata2), .in1(bit_extender_1_out), .out(multiplexer_5_out),
    .sel(control_1_alusrc));  // open: en
  ALUControl alucontrol_1 (.in_1(control_1_aluop2), .in_2(n26bitrom_1_instruction[4:0]), .out_3(alucontrol_1_out_3));
  Multiplexer #(.width(26)) multiplexer_6 (
    .in0(multiplexer_4_out), .in1(multiplexer_1_out), .out(multiplexer_6_out), .sel(control_1_jump));  // open: en
  ALU alu_1 (
    .a(n16x26_regfile_1_readdata1), .b(multiplexer_5_out), .out_5(alu_1_out_5),
    .ALU_Control(alucontrol_1_out_3), .zero(alu_1_zero));
  Multiplexer #(.width(26)) multiplexer_7 (
    .in0(multiplexer_6_out), .in1(n16x26_regfile_1_readdata1), .out(multiplexer_7_out), .sel(control_1_jr));  // open: en
  _26bitRAM u_26bitram_1 (
    .MemWrite(control_1_memwrite), .Address(alu_1_out_5), .Write_Data(n16x26_regfile_1_readdata2),
    .MemRead(control_1_memread), .Clk(clock_1_out), .Read_Data(n26bitram_1_read_data));
  Multiplexer #(.width(26)) multiplexer_8 (
    .in0(alu_1_out_5), .in1(n26bitram_1_read_data), .out(multiplexer_8_out), .sel(control_1_memtoreg));  // open: en
endmodule

module Control (
  input  [3:0] OpCode,
  output RegDst,
  output Jump,
  output Branch,
  output MemRead,
  output MemToReg,
  output MemWrite,
  output ALUSrc,
  output RegWrite,
  output jr,
  output jal,
  output ALUOp1,
  output ALUOP2
);

  wire and_6_out, and_7_out, and_8_out, not_1_out, not_2_out, not_3_out, not_4_out, not_5_out, not_6_out,
       not_7_out, not_8_out, not_9_out, not_10_out, not_11_out, not_12_out, not_13_out, not_14_out;

  not not_1 (not_1_out, OpCode[3]);
  not not_2 (not_2_out, OpCode[1]);
  not not_3 (not_3_out, OpCode[0]);
  not not_4 (not_4_out, OpCode[3]);
  not not_5 (not_5_out, OpCode[2]);
  and and_1 (MemWrite, OpCode[3], OpCode[1]);
  or or_1 (ALUSrc, OpCode[1], OpCode[3]);
  not not_6 (not_6_out, OpCode[2]);
  not not_7 (not_7_out, OpCode[1]);
  not not_8 (not_8_out, OpCode[3]);
  not not_9 (not_9_out, OpCode[2]);
  not not_10 (not_10_out, OpCode[0]);
  and and_2 (jr, OpCode[2], OpCode[0]);
  not not_11 (not_11_out, OpCode[0]);
  not not_12 (not_12_out, OpCode[3]);
  not not_13 (not_13_out, OpCode[2]);
  not not_14 (not_14_out, OpCode[1]);
  and and_3 (RegDst, not_1_out, not_2_out);
  and and_4 (Jump, OpCode[1], not_3_out);
  and and_5 (MemRead, not_4_out, not_5_out, OpCode[0]);
  and and_6 (and_6_out, not_6_out, not_7_out);
  and and_7 (and_7_out, not_8_out, not_9_out, OpCode[0]);
  and and_8 (and_8_out, OpCode[2], OpCode[1], not_10_out);
  and and_9 (jal, OpCode[2], OpCode[1], not_11_out);
  and and_10 (ALUOp1, not_12_out, not_13_out, not_14_out);
  or or_2 (RegWrite, and_6_out, and_7_out, and_8_out);

  assign ALUOP2 = OpCode[2];
  assign Branch = OpCode[2];
  assign MemToReg = OpCode[1];
endmodule

module ALUControl (
  input  [1:0] in_1,
  input  [4:0] in_2,
  output [4:0] out_3
);

  wire and_4_out, not_1_out;

  and and_1 (out_3[4], in_1[1], in_2[4]);
  and and_2 (out_3[3], in_1[1], in_2[3]);
  and and_3 (out_3[2], in_1[1], in_2[2]);
  not not_1 (not_1_out, in_1[1]);
  or or_1 (out_3[1], not_1_out, in_2[1]);
  and and_4 (and_4_out, in_1[1], in_2[0]);
  or or_2 (out_3[0], in_1[0], and_4_out);
endmodule
